# Fritzing sketch DefaultConnection (saved by Fritzing 0.9.3b)
breadboards: 1

parts:
  Raspberry_Pi_1 = Raspberry Pi 3 [part_number=RPI-3-V1.2]  # not connected
  Part1 = Arduino Uno (Rev3) - ICSP
  Part2 = Soil Moisture Sensor
  Capacitive_Soil_Moisture_Sensor1 = DFRobot Capacitive Soil Moisture Sensor V1.0 [part_number=SEN0193]

nets:
  N1: Part1.A0, Capacitive_Soil_Moisture_Sensor1.A
  N2: Part1.A2, Part2.SIG
  VCC: Part1.5V, Part2.VCC, Capacitive_Soil_Moisture_Sensor1.VCC
  GND: Part1.GND, Part2.GND, Capacitive_Soil_Moisture_Sensor1.GND

custom parts:
  DFRobot Capacitive Soil Moisture Sensor V1.0: DFRobot Capacitive Soil Moisture Sensor V1.0 This product measures soil moisture levels by capacitive sensing, rather than resistive sensing like other types of moisture sensor. It is made of a corrosion resistant material giving it a long service life. Insert it into soil and impress your friends with the real-time soil moisture data! The product includes an on-board voltage regulator which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
