# Fritzing sketch DefaultConnectionLora (saved by Fritzing 0.9.3b)
breadboards: 1

parts:
  Raspberry_Pi_1 = Raspberry Pi 3 [part_number=RPI-3-V1.2]
  Part1 = Arduino Uno (Rev3) - ICSP
  Part2 = Soil Moisture Sensor
  Capacitive_Soil_Moisture_Sensor1 = DFRobot Capacitive Soil Moisture Sensor V1.0 [part_number=SEN0193]
  Part3 = Adafruit RFM9x LoRa Radio [part_number="Adafruit #3072 and #3073"]
  Part4 = Adafruit RFM9x LoRa Radio [part_number="Adafruit #3072 and #3073"]

nets:
  3V3: Raspberry_Pi_1.3v3, Part4.VIN
  N1: Raspberry_Pi_1.GIPO4, Part4.DIO0
  N2: Raspberry_Pi_1.GIPO17, Part4.DIO1
  N3: Raspberry_Pi_1.GIPO27, Part4.DIO3
  N4: Raspberry_Pi_1.GIPO22, Part4.RST
  N5: Raspberry_Pi_1.GIPO10, Part4.MOSI
  N6: Raspberry_Pi_1.GIPO9, Part4.MISO
  N7: Raspberry_Pi_1.GIPO11, Part4.SCK
  N8: Raspberry_Pi_1.GIPO8, Part4.EN
  N9: Raspberry_Pi_1.GIPO18, Part4.DIO2
  GND: Raspberry_Pi_1.GND, Part4.GND
  N10: Part1.A0, Capacitive_Soil_Moisture_Sensor1.A
  N11: Part1.A2, Part2.SIG
  N12: Part1.D9_PWM, Part3.RST
  N13: Part1.D10_PWM/SS, Part3.EN
  N14: Part1.D11_PWM/MOSI, Part3.MOSI
  N15: Part1.D12/MISO, Part3.MISO
  N16: Part1.D13/SCK, Part3.SCK
  N17: Part1.D2, Part3.DIO0
  3V3_2: Part1.3V3, Part3.VIN
  VCC: Part1.5V, Part2.VCC, Capacitive_Soil_Moisture_Sensor1.VCC
  GND_2: Part1.GND, Part2.GND, Capacitive_Soil_Moisture_Sensor1.GND, Part3.GND

custom parts:
  DFRobot Capacitive Soil Moisture Sensor V1.0: DFRobot Capacitive Soil Moisture Sensor V1.0 This product measures soil moisture levels by capacitive sensing, rather than resistive sensing like other types of moisture sensor. It is made of a corrosion resistant material giving it a long service life. Insert it into soil and impress your friends with the real-time soil moisture data! The product includes an on-board voltage regulator which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
  Adafruit RFM9x LoRa Radio: Sending data over long distances is like magic, and now you can be a magician with this range of powerful and easy-to-use radio modules. Sure, sometimes you want to talk to a computer (a good time to use WiFi) or perhaps communicate with a Phone (choose Bluetooth Low Energy!) but what if you want to send data very far? Most WiFi, Bluetooth, Zigbee and other wireless chipsets use 2.4GHz, which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
